# Fritzing sketch banners (saved by Fritzing 1.0.3b)
circuit board: 8.73595cm x 6.43364cm
breadboards: 2

parts:
  Power_plug2 = Power plug
  100uF = Electrolytic Capacitor [capacitance=0.1mF voltage=35V package="100 mil [THT, electrolytic]"]
  104 = Ceramic Capacitor [capacitance=100nF voltage=16V package="200 mil [THT, multilayer]"]
  input = double row female pin header, 4 pins [form="♀ (female)"]
  LDR = double row female pin header, 4 pins [form="♀ (female)"]
  Depth = LED - 3mm [color="Red (635nm)" current=0.030A package="3 mm [THT]"]
  1K = Resistor [tolerance=±5% resistance=1k power=0.25W package=THT]
  LDR1 = Photocell (LDR) [power=0.25W dark_resistance_@0.01lx=300kΩ light_resistance_@100lx=400Ω luminance=10lx package=THT]
  LED = female pin header, 2 pins [form="♀ (female)"]
  100K = Rotary Potentiometer (Small) [maximum_resistance=100kΩ knob_status=50% power=0.5W package=THT]
  100K_2 = Rotary Potentiometer (Small) [maximum_resistance=100kΩ knob_status=50% power=0.5W package=THT]
  10K = Rotary Potentiometer (Small) [maximum_resistance=10kΩ knob_status=50% power=0.5W package=THT]
  100K_3 = Rotary Potentiometer (Small) [maximum_resistance=100kΩ knob_status=50% power=0.5W package=THT]
  out = Audio Jack (TRS) 3.5mm [package="PG203J [THT]"]
  out_2 = double row female pin header, 2 pins [form="♀ (female)"]
  LED6 = LED - 3mm [color="Red (635nm)" current=0.030A package="3 mm [THT]"]
  1K_2 = Resistor [tolerance=±5% resistance=1k power=0.25W package=THT]
  LDR2 = double row female pin header, 4 pins [form="♀ (female)"]
  LDR3 = Photocell (LDR) [power=0.25W dark_resistance_@0.01lx=300kΩ light_resistance_@100lx=400Ω luminance=10lx package=THT]
  Input = Audio Jack (TRS) 3.5mm [package="PG203J [THT]"]
  074 = TL074 Quad Opamp (Movable) [package="DIP (Dual Inline)"]
  074_PWR = TL074 Quad Opamp (Movable) [package="DIP (Dual Inline)"]  # not connected
  074_A = TL074 Quad Opamp (Movable) [package="DIP (Dual Inline)"]
  074_B = TL074 Quad Opamp (Movable) [package="DIP (Dual Inline)"]
  074_C = TL074 Quad Opamp (Movable) [package="DIP (Dual Inline)"]
  074_D = TL074 Quad Opamp (Movable) [package="DIP (Dual Inline)"]  # not connected
  074_2 = TL074 Quad Opamp (Movable) [package="DIP (Dual Inline)"]
  074_PWR_2 = TL074 Quad Opamp (Movable) [package="DIP (Dual Inline)"]
  074_A_2 = TL074 Quad Opamp (Movable) [package="DIP (Dual Inline)"]
  074_B_2 = TL074 Quad Opamp (Movable) [package="DIP (Dual Inline)"]  # not connected
  074_C_2 = TL074 Quad Opamp (Movable) [package="DIP (Dual Inline)"]  # not connected
  074_D_2 = TL074 Quad Opamp (Movable) [package="DIP (Dual Inline)"]
  47K = Resistor [tolerance=±5% resistance=47k power=0.25W package=THT]
  Jm8 = female pin header, 3 pins [form="♀ (female)"]
  Jm9 = female pin header, 3 pins [form="♀ (female)"]
  Jm10 = female pin header, 3 pins [form="♀ (female)"]
  +v = female pin header, 2 pins [form="♀ (female)"]
  47K_2 = Resistor [tolerance=±5% resistance=47k power=0.25W package=THT]
  5817 = Schottky Diode [part_number=1N5817 package="300 mil [THT]"]
  47K_3 = Resistor [tolerance=±5% resistance=47k power=0.25W package=THT]
  22K = Resistor [tolerance=±5% resistance=22k power=0.25W package=THT]
  220K = Resistor [tolerance=±5% resistance=220k power=0.25W package=THT]
  Speed = LED - 3mm [color="Red (635nm)" current=0.030A package="3 mm [THT]"]
  1K_3 = Resistor [tolerance=±5% resistance=1k power=0.25W package=THT]
  47K_4 = Resistor [tolerance=±5% resistance=47k power=0.25W package=THT]
  LED8 = female pin header, 1 pin [form="♀ (female)"]
  D1 = Diode [package=diode-1n4148]
  D2 = Diode [package=diode-1n4148]
  33K = Resistor [tolerance=±5% resistance=33k power=0.25W package=THT]
  330K = Resistor [tolerance=±5% resistance=330k power=0.25W package=THT]
  33K_2 = Resistor [tolerance=±5% resistance=33k power=0.25W package=THT]
  1M = Resistor [tolerance=±5% resistance=1M power=0.25W package=THT]
  22K_2 = Resistor [tolerance=±5% resistance=22k power=0.25W package=THT]
  120K = Resistor [tolerance=±5% resistance=150k power=0.25W package=THT]
  47K_5 = Resistor [tolerance=±5% resistance=47k power=0.25W package=THT]
  S1 = lock switch 8x8
  Jm11 = female pin header, 3 pins [form="♀ (female)"]  # not connected
  LED10 = female pin header, 1 pin [form="♀ (female)"]
  S2 = lock switch 8x8
  Jm12 = female pin header, 3 pins [form="♀ (female)"]  # not connected
  4_7k = Resistor [tolerance=±5% resistance=4.7k power=0.25W package=THT]
  Jm7 = female pin header, 3 pins [form="♀ (female)"]
  33K1 = Resistor [tolerance=±5% resistance=33k power=0.25W package=THT]
  470K = Resistor [tolerance=±5% resistance=470k power=0.25W package=THT]
  470K_2 = Resistor [tolerance=±5% resistance=470k power=0.25W package=THT]
  104_2 = Ceramic Capacitor [capacitance=100nF voltage=16V package="200 mil [THT, multilayer]"]
  470K1 = Resistor [tolerance=±5% resistance=470k power=0.25W package=THT]
  2_2K = Resistor [tolerance=±5% resistance=2.2k power=0.25W package=THT]

nets:
  GND: Power_plug2.GND, 100uF.-, 104.1, 1K.Pin_1, out.Sleeve, out_2.pin1, 1K_2.Pin_1, Input.Sleeve, 074.connector10, 074_2.connector10, 074_PWR_2.VCC-, Speed.cathode, 47K_4.Pin_1, S1.Pin_5, 470K.Pin_1
  N1: Power_plug2.VCC, 5817.anode
  N2: 100uF.+, 104.0, 100K_3.leg2, 074.connector3, 074_2.connector3, Jm10.pin1, +v.pin1, +v.pin2, 5817.cathode, 470K_2.Pin_1
  N3: input.pin1, input.pin2, Input.Tip
  N4: input.pin3, input.pin4, Input.Ring, 47K.Pin_1
  N5: LDR.pin1, LDR.pin2, LDR1.pin_1, 47K_3.Pin_1
  N6: LDR.pin3, LDR.pin4, LDR1.pin_0, 100K_3.wiper, Jm10.pin2
  N7: Depth.cathode, 1K.Pin_0
  N8: Depth.anode, LED.pin1, LED.pin2, 10K.leg1, Jm9.pin3
  N9: 100K.leg1, D2.A, Jm7.pin3
  N10: 100K.wiper, Jm7.pin2
  N11: 100K.leg2, D1.C, Jm7.pin1
  N12: 100K_2.leg1, Jm8.pin3, 2_2K.Pin_0
  N13: 100K_2.wiper, Jm8.pin2, 470K1.Pin_0
  N14: 100K_2.leg2, 074.connector0, Jm8.pin1, D1.A, D2.C, 47K_5.Pin_1
  N15: 10K.wiper, 10K.leg2, Jm9.pin1, Jm9.pin2, 4_7k.Pin_0
  N16: 100K_3.leg1, Jm10.pin3, S1.Pin_4
  N17: out.Ring, out.Tip, out_2.pin2, 47K_2.Pin_0
  N18: LED6.cathode, 1K_2.Pin_0
  N19: LDR2.pin1, LDR2.pin2, LDR3.pin_1
  N20: LDR2.pin3, LDR2.pin4, LDR3.pin_0
  N21: 074.connector1, 074.connector4, 074.connector7, 074.connector8, 2_2K.Pin_1
  N22: 074.connector2, 47K_5.Pin_0, 33K1.Pin_1
  N23: 074.connector5, 104_2.1, 470K1.Pin_1
  N24: 074.connector6, 074.connector11, 4_7k.Pin_1, 33K1.Pin_0, 104_2.0
  N25: 074.connector9, 470K.Pin_0, 470K_2.Pin_0
  N26: 074.connector12, 074.connector13, 1K_3.Pin_0
  N27: 074_A.1IN-, 074_B.2IN+, 074_C.3OUT
  N28: 074_2.connector0, 220K.Pin_0
  N29: 074_2.connector1, 47K.Pin_0, 22K.Pin_0
  N30: 074_2.connector2, 074_2.connector9, 074_2.connector11, 47K_3.Pin_0, 47K_4.Pin_0, 33K_2.Pin_1
  N31: 074_2.connector4, 22K_2.Pin_0, S2.Pin_5
  N32: 074_2.connector5, 33K_2.Pin_0, 120K.Pin_1
  N33: 074_2.connector6, 47K_2.Pin_1, 120K.Pin_0
  N34: 074_2.connector7, 1M.Pin_1
  N35: 074_2.connector8, 33K.Pin_0, 330K.Pin_0, 22K_2.Pin_1
  N36: 074_2.connector12, 22K.Pin_1, 220K.Pin_1, 33K.Pin_1
  N37: 074_2.connector13, 330K.Pin_1
  N38: 074_A_2.1IN+, 074_D_2.4IN+
  N39: Speed.anode, 1K_3.Pin_1
  N40: LED8.pin1, S1.Pin_6
  N41: 1M.Pin_0, S2.Pin_6
  N42: LED10.pin1, S2.Pin_4

notes:
  banners
  jlcjlcjlcjlc
  blueprint@poetaster.de 2024

custom parts:
  TL074 Quad Opamp (Movable): Quadruple Operational Amplifier (Opamp)
  TL074 Quad Opamp (Movable): Quadruple Operational Amplifier (Opamp)
  TL074 Quad Opamp (Movable): Quadruple Operational Amplifier (Opamp)
  TL074 Quad Opamp (Movable): Quadruple Operational Amplifier (Opamp)
  TL074 Quad Opamp (Movable): Quadruple Operational Amplifier (Opamp)
  TL074 Quad Opamp (Movable): Quadruple Operational Amplifier (Opamp)
  lock switch 8x8: lock switch 8x8.
